# Fritzing sketch Tank (saved by Fritzing 0.9.5d)
breadboards: 2

parts:
  MCU1 = Raspberry Pi Zero
  U1 = LIPO-1000mAh [package=lipo-1000]  # not connected
  U2 = LIPO-1000mAh [package=lipo-1000]  # not connected
  J1 = Basic Servo
  M1 = DC Motor  # not connected
  M2 = DC Motor  # not connected

nets:
  N1: MCU1.pin_1, MCU1.pin_17, J1.vcc
  N2: MCU1.pin_20, MCU1.pin_25, MCU1.pin_30, MCU1.pin_34, J1.gnd
  N3: MCU1.pin_35, J1.pulse

notes:
  (5V USB step-up converter)
  1
  2
  3
  4
  USB
  +
  -
  (DRV8833 Dual channer motor driver)
  GND
  VIN
  OUT1
  OUT2
  OUT3
  OUT4
  B1-IN
  B2-IN
  A2-IN
  A1-IN
  EF90D 360
  3.3V
  Raspberry power supply
  Motors, motor driver, motor power supply
  Turret servo
  Tank wiring diagram
  (empty)
